# Fritzing sketch RTKRover (saved by Fritzing 0.9.9b)
breadboards: 1

parts:
  Part1 = Adafruit HUZZAH32 ESP32 Feather [part_number="Adafruit #3405"]
  Qwiic1_BNO080 = Qwiic Connector  # not connected
  10_k = Resistor [tolerance=±5% power=0.25 resistance=220 package=THT]
  Wipe = Pushbutton [package="[SMD]"]
  S4 = Toggle Switch [package=THT]
  BAT1 = Battery Holders [package=lipo-1100mAh]
  Reset = Pushbutton [package="[SMD]"]
  10_k_2 = Resistor [tolerance=±5% power=0.25 resistance=220 package=THT]
  Qwiic2_RTK-SMA = Qwiic Connector  # not connected

nets:
  N1: Part1.GND, 10_k.Pin_1, BAT1.-, 10_k_2.Pin_1
  N2: Part1.3.3V, Reset.Pin_1, Reset.Pin_2
  N3: Part1.VBAT, S4.COM
  N4: Part1.EN, Reset.Pin_3, Reset.Pin_4, 10_k_2.Pin_0
  N5: Part1.IO15_A8, 10_k.Pin_0, Wipe.Pin_3, Wipe.Pin_4
  N6: Wipe.Pin_1, Wipe.Pin_2
  N7: S4.L2, BAT1.+

custom parts:
  Qwiic Connector: Qwiic PCB connector
